// Logisim project cpuB.circ as structural Verilog: 9 circuits, main circuit main
module main (
  input  reset,
  output [31:0] Instr,
  output [31:0] PC,
  output RegWrite,
  output [4:0] RegAddr,
  output [31:0] RegData,
  output MemWrite,
  output [31:0] MemAddr,
  output [31:0] MemData
);

  wire ALUSrc, and_1_out, Branch, clk_out, ExtOp, Jump, Link, MemRead, MemToReg, RegDst, ZeroSign;
  wire [2:0] ALUop;
  wire [4:0] multiplexer_1_out, rd, rs, rt;
  wire [5:0] funct, opCode;
  wire [15:0] immediate;
  wire [25:0] instr_index;
  wire [31:0] dm_out, extended, grf_1_rd1, multiplexer_3_out, multiplexer_4_out, nPC;

  Clock clk (.out(clk_out));
  and and_1 (and_1_out, ZeroSign, Branch);
  ifu ifu (
    .clk(clk_out), .reset(reset), .Branch(and_1_out), .offset(immediate), .Jump(Jump),
    .instr_index(instr_index), .curPC(PC), .nextPC(nPC), .instr(Instr));
  instr_decode instr_decode (
    .instr(Instr), .opCode(opCode), .funct(funct), .immediate(immediate), .instr_index(instr_index), .rs(rs),
    .rt(rt), .rd(rd));
  extend sign_extend (.in(immediate), .op(ExtOp), .out(extended));
  control controller (
    .op(opCode), .funct(funct), .RegDst(RegDst), .ALUSrc(ALUSrc), .MemToReg(MemToReg), .RegWrite(RegWrite),
    .MemRead(MemRead), .MemWrite(MemWrite), .Branch(Branch), .ExtOp(ExtOp), .Jump(Jump), .Link(Link),
    .ALUOp(ALUop));
  Multiplexer #(.width(5)) multiplexer_1 (.in0(rt), .in1(rd), .out(multiplexer_1_out), .sel(RegDst));  // open: en
  Multiplexer #(.width(5)) multiplexer_2 (
    .in0(multiplexer_1_out), .in1({5{1'b1}}), .out(RegAddr), .sel(Link));  // open: en
  grf grf_1 (
    .A1(rs), .A2(rt), .A3(RegAddr), .WD(RegData), .clk(clk_out), .reset(reset), .WE(RegWrite),
    .RD1(grf_1_rd1), .RD2(MemData));
  // Probe on Instr
  // Probe on PC
  Multiplexer #(.width(32)) multiplexer_3 (
    .in0(MemData), .in1(extended), .out(multiplexer_3_out), .sel(ALUSrc));  // open: en
  Multiplexer #(.width(32)) multiplexer_4 (
    .in0(multiplexer_3_out), .in1(nPC), .out(multiplexer_4_out), .sel(Link));  // open: en
  Multiplexer #(.width(32)) multiplexer_5 (.in0(MemAddr), .in1(dm_out), .out(RegData), .sel(MemToReg));  // open: en
  alu alu (.A(grf_1_rd1), .B(multiplexer_4_out), .op(ALUop), .zero(ZeroSign), .out(MemAddr));
  // Probe on nPC
  dm dm (
    .clk(clk_out), .reset(reset), .write_enable(MemWrite), .read_enable(MemRead), .read_address(MemAddr),
    .write_data(MemData), .out(dm_out));
endmodule

module grf (
  input  clk,
  input  reset,
  input  WE,
  input  [4:0] A1,
  input  [4:0] A2,
  input  [4:0] A3,
  input  [31:0] WD,
  output [31:0] RD1,
  output [31:0] RD2
);

  wire [31:0] in0, in1, in2, in3, in4, in5, in6, in7, in8, in9, in10, in11, in12, in13, in14, in15, in16,
       in17, in18, in19, in20, in21, in22, in23, in24, in25, in26, in27, in28, in29, in30, in31, val0, val1,
       val2, val3, val4, val5, val6, val7, val8, val9, val10, val11, val12, val13, val14, val15, val16,
       val17, val18, val19, val20, val21, val22, val23, val24, val25, val26, val27, val28, val29, val30,
       val31;

  Demultiplexer #(.select(5), .width(32), .tristate("true")) demultiplexer_1 (
    .out0(in0), .out1(in1), .out2(in2), .out3(in3), .out4(in4), .out5(in5), .out6(in6), .out7(in7),
    .out8(in8), .out9(in9), .out10(in10), .out11(in11), .out12(in12), .out13(in13), .out14(in14),
    .out15(in15), .out16(in16), .out17(in17), .out18(in18), .out19(in19), .out20(in20), .out21(in21),
    .out22(in22), .out23(in23), .out24(in24), .out25(in25), .out26(in26), .out27(in27), .out28(in28),
    .out29(in29), .out30(in30), .out31(in31), .in(WD), .sel(A3));  // open: en
  Register #(.width(32)) register_1 (.D({32{1'b0}}), .en(WE), .Q(val0), .clk(clk), .clr(reset));
  Register #(.width(32)) register_2 (.D(in1), .en(WE), .Q(val1), .clk(clk), .clr(reset));
  Register #(.width(32)) register_3 (.D(in2), .en(WE), .Q(val2), .clk(clk), .clr(reset));
  Register #(.width(32)) register_4 (.D(in3), .en(WE), .Q(val3), .clk(clk), .clr(reset));
  Register #(.width(32)) register_5 (.D(in4), .en(WE), .Q(val4), .clk(clk), .clr(reset));
  Register #(.width(32)) register_6 (.D(in20), .en(WE), .Q(val20), .clk(clk), .clr(reset));
  Register #(.width(32)) register_7 (.D(in21), .en(WE), .Q(val21), .clk(clk), .clr(reset));
  Register #(.width(32)) register_8 (.D(in22), .en(WE), .Q(val22), .clk(clk), .clr(reset));
  Register #(.width(32)) register_9 (.D(in5), .en(WE), .Q(val5), .clk(clk), .clr(reset));
  Register #(.width(32)) register_10 (.D(in6), .en(WE), .Q(val6), .clk(clk), .clr(reset));
  Register #(.width(32)) register_11 (.D(in7), .en(WE), .Q(val7), .clk(clk), .clr(reset));
  Register #(.width(32)) register_12 (.D(in8), .en(WE), .Q(val8), .clk(clk), .clr(reset));
  Register #(.width(32)) register_13 (.D(in9), .en(WE), .Q(val9), .clk(clk), .clr(reset));
  Register #(.width(32)) register_14 (.D(in23), .en(WE), .Q(val23), .clk(clk), .clr(reset));
  Register #(.width(32)) register_15 (.D(in24), .en(WE), .Q(val24), .clk(clk), .clr(reset));
  Register #(.width(32)) register_16 (.D(in25), .en(WE), .Q(val25), .clk(clk), .clr(reset));
  Register #(.width(32)) register_17 (.D(in10), .en(WE), .Q(val10), .clk(clk), .clr(reset));
  Register #(.width(32)) register_18 (.D(in11), .en(WE), .Q(val11), .clk(clk), .clr(reset));
  Register #(.width(32)) register_19 (.D(in12), .en(WE), .Q(val12), .clk(clk), .clr(reset));
  Register #(.width(32)) register_20 (.D(in13), .en(WE), .Q(val13), .clk(clk), .clr(reset));
  Register #(.width(32)) register_21 (.D(in14), .en(WE), .Q(val14), .clk(clk), .clr(reset));
  Register #(.width(32)) register_22 (.D(in26), .en(WE), .Q(val26), .clk(clk), .clr(reset));
  Register #(.width(32)) register_23 (.D(in27), .en(WE), .Q(val27), .clk(clk), .clr(reset));
  Register #(.width(32)) register_24 (.D(in28), .en(WE), .Q(val28), .clk(clk), .clr(reset));
  Register #(.width(32)) register_25 (.D(in15), .en(WE), .Q(val15), .clk(clk), .clr(reset));
  Register #(.width(32)) register_26 (.D(in16), .en(WE), .Q(val16), .clk(clk), .clr(reset));
  Register #(.width(32)) register_27 (.D(in17), .en(WE), .Q(val17), .clk(clk), .clr(reset));
  Register #(.width(32)) register_28 (.D(in18), .en(WE), .Q(val18), .clk(clk), .clr(reset));
  Register #(.width(32)) register_29 (.D(in19), .en(WE), .Q(val19), .clk(clk), .clr(reset));
  Register #(.width(32)) register_30 (.D(in29), .en(WE), .Q(val29), .clk(clk), .clr(reset));
  Register #(.width(32)) register_31 (.D(in30), .en(WE), .Q(val30), .clk(clk), .clr(reset));
  Register #(.width(32)) register_32 (.D(in31), .en(WE), .Q(val31), .clk(clk), .clr(reset));
  Multiplexer #(.select(5), .width(32)) multiplexer_1 (
    .in0(val0), .in1(val1), .in2(val2), .in3(val3), .in4(val4), .in5(val5), .in6(val6), .in7(val7),
    .in8(val8), .in9(val9), .in10(val10), .in11(val11), .in12(val12), .in13(val13), .in14(val14),
    .in15(val15), .in16(val16), .in17(val17), .in18(val18), .in19(val19), .in20(val20), .in21(val21),
    .in22(val22), .in23(val23), .in24(val24), .in25(val25), .in26(val26), .in27(val27), .in28(val28),
    .in29(val29), .in30(val30), .in31(val31), .out(RD1), .sel(A1));  // open: en
  Multiplexer #(.select(5), .width(32)) multiplexer_2 (
    .in0(val0), .in1(val1), .in2(val2), .in3(val3), .in4(val4), .in5(val5), .in6(val6), .in7(val7),
    .in8(val8), .in9(val9), .in10(val10), .in11(val11), .in12(val12), .in13(val13), .in14(val14),
    .in15(val15), .in16(val16), .in17(val17), .in18(val18), .in19(val19), .in20(val20), .in21(val21),
    .in22(val22), .in23(val23), .in24(val24), .in25(val25), .in26(val26), .in27(val27), .in28(val28),
    .in29(val29), .in30(val30), .in31(val31), .out(RD2), .sel(A2));  // open: en
endmodule

module extend (
  input  [15:0] in,
  input  op,
  output [31:0] out
);

  wire [31:0] bit_extender_1_out, bit_extender_2_out;

  assign bit_extender_1_out = {{16{1'b0}}, in};  // Bit_Extender bit_extender_1
  assign bit_extender_2_out = {{16{in[15]}}, in};  // Bit_Extender bit_extender_2
  Multiplexer #(.width(32)) multiplexer_1 (
    .in0(bit_extender_1_out), .in1(bit_extender_2_out), .out(out), .sel(op));  // open: en
endmodule

module dm (
  input  clk,
  input  reset,
  input  write_enable,
  input  read_enable,
  input  [31:0] read_address,
  input  [31:0] write_data,
  output [31:0] out
);

  wire [15:0] bitselector_1_out;

  BitSelector #(.width(32), .group(16)) bitselector_1 (.in(read_address), .out(bitselector_1_out), .sel(1'b0));
  RAM #(.addrWidth(16), .dataWidth(32), .bus("separate")) ram_1 (
    .addr(bitselector_1_out), .din(write_data), .data(out), .str(write_enable), .sel(1'b1), .clk(clk),
    .ld(read_enable), .clr(reset));
endmodule

module alu (
  input  [31:0] A,
  input  [31:0] B,
  input  [2:0] op,
  output zero,
  output [31:0] out
);

  wire [4:0] bitselector_1_out;
  wire [31:0] adder_1_out, adder_2_out, or_1_out, shifter_1_out, shifter_2_out, subtractor_1_out;

  Adder #(.width(32)) adder_1 (.a(A), .b(B), .out(adder_1_out));  // open: cin, cout
  Subtractor #(.width(32)) subtractor_1 (.a(A), .b(B), .out(subtractor_1_out));  // open: bin, bout
  assign or_1_out = A | B;  // OR_Gate or_1, 32 bits wide
  BitSelector #(.width(32), .group(5)) bitselector_1 (.in(B), .out(bitselector_1_out), .sel(3'b000));
  Shifter #(.width(32)) shifter_1 (.in(A), .\dist (bitselector_1_out), .out(shifter_1_out));
  Shifter #(.width(32)) shifter_2 (.in(B), .\dist (5'b10000), .out(shifter_2_out));
  Adder #(.width(32)) adder_2 (.a(B), .b(32'h4), .out(adder_2_out));  // open: cin, cout
  Multiplexer #(.select(3), .width(32)) multiplexer_1 (
    .in0(adder_1_out), .in1(subtractor_1_out), .in2(or_1_out), .in3(shifter_1_out), .in4(shifter_2_out),
    .in5(adder_2_out), .out(out), .sel(op));  // open: in6, in7, en
  Comparator #(.width(32)) comparator_1 (.a({32{1'b0}}), .b(out), .eq(zero));  // open: gt, lt
endmodule

module ifu (
  input  clk,
  input  reset,
  input  Branch,
  input  [15:0] offset,
  input  Jump,
  input  [25:0] instr_index,
  output [31:0] curPC,
  output [31:0] nextPC,
  output [31:0] instr
);

  wire [11:0] bitselector_1_out;
  wire [31:0] adder_2_out, adder_3_out, multiplexer_1_out, offset_t, register_1_q, shifter_1_out,
       subtractor_1_out;

  Subtractor #(.width(32)) subtractor_1 (.a(nextPC), .b(32'h3000), .out(subtractor_1_out));  // open: bin, bout
  assign offset_t = {{14{offset[15]}}, {offset, 2'b00}};  // Bit_Extender bit_extender_1
  Register #(.width(32)) register_1 (.D(subtractor_1_out), .Q(register_1_q), .clk(clk), .clr(reset));  // open: en
  Adder #(.width(32)) adder_1 (.a(register_1_q), .b(32'h3000), .out(curPC));  // open: cin, cout
  Adder #(.width(32)) adder_2 (.a(register_1_q), .b(32'h3004), .out(adder_2_out));  // open: cin, cout
  Shifter #(.width(32), .shift("lr")) shifter_1 (.in(register_1_q), .\dist (5'b00010), .out(shifter_1_out));
  BitSelector #(.width(32), .group(12)) bitselector_1 (.in(shifter_1_out), .out(bitselector_1_out), .sel(2'b00));
  Multiplexer #(.width(32)) multiplexer_1 (
    .in0(adder_2_out), .in1(adder_3_out), .out(multiplexer_1_out), .sel(Branch));  // open: en
  Adder #(.width(32)) adder_3 (.a(adder_2_out), .b(offset_t), .out(adder_3_out));  // open: cin, cout
  ROM #(.addrWidth(12), .dataWidth(32)) rom_1 (.addr(bitselector_1_out), .data(instr), .sel(1'b1));
  Multiplexer #(.width(32)) multiplexer_2 (
    .in0(multiplexer_1_out), .in1({curPC[31:28], instr_index, 2'b00}), .out(nextPC), .sel(Jump));  // open: en

  // Other names for the same wires on the sheet: instr_index_t[31:2] = {curPC[31:28], instr_index}

  // Notes on the sheet:
  //   contents of rom_1 (hex, n*v repeats v):
  //   3c000001 3c020006 3c030009 3c04000b 3c050001 3c060001 3c07000c 3c08000e 3c09000e 3c0a000b 3c0b0001
  //   3c0c0002 3c0d0003 3c0e000b 3c0f0003 3c10000a 3c110002 3c12000b 3c130008 3c140010 3c150005 3c160008
  //   3c170000 3c180005 3c19000d 3c1a000b 3c1b0007 3c1c0004 3c1d0004 3c1e000a 3c1f000a 03d94022 8c0c08b4
  //   02b5e020 1263fffe 00000000 03bb2822 02623022 033df820 01276022 ac1d0dec 01889822 03cae822 02b82820
  //   03127820 009c9822 ac080500 03428022 008fa022 8c180d18 0208e020 02aaa822 00df3820 ac070508 8c190748
  //   3c1c09fa 3c0449d1 006d5022 03196822 00f9c822 10a9003d 02f21022 038ba820 00f79022 020b2822 02f45822
  //   12600000 11e4ffff 00000000 133c0036 ac080eac 0330f820 8c0b0c80 0122b822 11b30017 8c170c00 02e72822
  //   00000000 013c2022 3c1d3a5a 03eaf822 01007022 00525022 01af9022 01399822 3c09f327 127c0023 8c1f0e8c
  //   035f5020 8c040b18 01ff3022 01fdb020 03b93020 02b5e020 00564020 02ac2820 01020020 006e2022 ac130330
  //   01dda022 11890015 01fc1822 ac190e54 03d3a822 026f5022 026d4020 0197c020 3c00c613 02e88822 8c0905b8
  //   00b4f820 3c08a698 ac0007a8 8c1a0f28 12580007 8c0f0708 00f7e822 00ffd022 00000000 115f0002 00000000
  //   ac0b06bc 8c0207f8 ac1803ac ac0303f0 008d2820 03072020 1010fffc ac14031c 02ce4822 03cd5020
endmodule

module control (
  input  [5:0] op,
  input  [5:0] funct,
  output RegDst,
  output ALUSrc,
  output MemToReg,
  output RegWrite,
  output MemRead,
  output MemWrite,
  output Branch,
  output ExtOp,
  output Jump,
  output Link,
  output [2:0] ALUOp
);

  wire add, beq, j, jal, lui, lw, nop, not_1_out, not_2_out, not_3_out, not_4_out, not_5_out, not_6_out,
       not_7_out, not_8_out, not_9_out, not_10_out, not_11_out, not_12_out, not_13_out, not_14_out,
       not_15_out, not_16_out, not_17_out, not_18_out, not_19_out, not_20_out, not_21_out, not_22_out,
       not_23_out, not_24_out, not_25_out, not_26_out, not_27_out, not_28_out, not_29_out, not_30_out,
       not_31_out, not_32_out, not_33_out, not_34_out, not_35_out, not_36_out, not_37_out, not_38_out,
       not_39_out, not_40_out, not_41_out, not_42_out, not_43_out, not_44_out, not_45_out, ori, special, sub,
       sw;
  wire [7:0] or_1_out;

  or or_1 (or_1_out[0], add, lw, sw);
  or or_2 (or_1_out[1], sub, beq);
  buf or_3 (or_1_out[2], ori);  // OR_Gate
  buf or_4 (or_1_out[3], nop);  // OR_Gate
  buf or_5 (or_1_out[4], lui);  // OR_Gate
  buf or_6 (or_1_out[5], jal);  // OR_Gate
  BitFinder bitfinder_1 (.in(or_1_out), .index(ALUOp));  // open: found
  not not_1 (not_1_out, op[5]);
  not not_2 (not_2_out, op[4]);
  not not_3 (not_3_out, op[3]);
  and u_special (special, not_1_out, not_2_out, not_3_out, not_4_out, not_5_out, not_6_out);
  not not_4 (not_4_out, op[2]);
  not not_5 (not_5_out, op[1]);
  not not_6 (not_6_out, op[0]);
  not not_7 (not_7_out, op[5]);
  not not_8 (not_8_out, op[4]);
  and u_ori (ori, not_7_out, not_8_out, op[3], op[2], not_9_out, op[0]);
  not not_9 (not_9_out, op[1]);
  not not_10 (not_10_out, op[4]);
  not not_11 (not_11_out, op[3]);
  and u_lw (lw, op[5], not_10_out, not_11_out, not_12_out, op[1], op[0]);
  not not_12 (not_12_out, op[2]);
  not not_13 (not_13_out, op[4]);
  and u_sw (sw, op[5], not_13_out, op[3], not_14_out, op[1], op[0]);
  not not_14 (not_14_out, op[2]);
  not not_15 (not_15_out, op[5]);
  not not_16 (not_16_out, op[4]);
  not not_17 (not_17_out, op[3]);
  and u_beq (beq, not_15_out, not_16_out, not_17_out, op[2], not_18_out, not_19_out);
  not not_18 (not_18_out, op[1]);
  not not_19 (not_19_out, op[0]);
  not not_20 (not_20_out, op[5]);
  not not_21 (not_21_out, op[4]);
  and u_lui (lui, not_20_out, not_21_out, op[3], op[2], op[1], op[0]);
  not not_22 (not_22_out, op[5]);
  not not_23 (not_23_out, op[4]);
  not not_24 (not_24_out, op[3]);
  and u_j (j, not_22_out, not_23_out, not_24_out, not_25_out, op[1], not_26_out);
  not not_25 (not_25_out, op[2]);
  not not_26 (not_26_out, op[0]);
  not not_27 (not_27_out, op[5]);
  not not_28 (not_28_out, op[4]);
  not not_29 (not_29_out, op[3]);
  and u_jal (jal, not_27_out, not_28_out, not_29_out, not_30_out, op[1], op[0]);
  not not_30 (not_30_out, op[2]);
  or or_7 (RegDst, add, sub);
  or or_8 (ALUSrc, ori, lw, sw, lui);
  buf or_9 (MemToReg, lw);  // OR_Gate
  or or_10 (RegWrite, add, sub, ori, lw, lui);
  buf or_11 (MemRead, lw);  // OR_Gate
  buf or_12 (MemWrite, sw);  // OR_Gate
  buf or_13 (Branch, beq);  // OR_Gate
  or or_14 (ExtOp, lw, sw, beq);
  buf or_15 (Jump, j);  // OR_Gate
  buf or_16 (Link, jal);  // OR_Gate
  not not_31 (not_31_out, funct[4]);
  not not_32 (not_32_out, funct[3]);
  and u_add (add, funct[5], not_31_out, not_32_out, special, not_33_out, not_34_out, not_35_out);
  not not_33 (not_33_out, funct[2]);
  not not_34 (not_34_out, funct[1]);
  not not_35 (not_35_out, funct[0]);
  not not_36 (not_36_out, funct[4]);
  not not_37 (not_37_out, funct[3]);
  and u_sub (sub, funct[5], not_36_out, not_37_out, special, not_38_out, funct[1], not_39_out);
  not not_38 (not_38_out, funct[2]);
  not not_39 (not_39_out, funct[0]);
  not not_40 (not_40_out, funct[5]);
  not not_41 (not_41_out, funct[4]);
  not not_42 (not_42_out, funct[3]);
  and u_nop (nop, not_40_out, not_41_out, not_42_out, special, not_43_out, not_44_out, not_45_out);
  not not_43 (not_43_out, funct[2]);
  not not_44 (not_44_out, funct[1]);
  not not_45 (not_45_out, funct[0]);
endmodule

module instr_decode (
  input  [31:0] instr,
  output [5:0] opCode,
  output [5:0] funct,
  output [15:0] immediate,
  output [25:0] instr_index,
  output [4:0] rs,
  output [4:0] rt,
  output [4:0] rd
);


  assign funct = instr[5:0];
  assign immediate = instr[15:0];
  assign instr_index = instr[25:0];
  assign opCode = instr[31:26];
  assign rd = instr[15:11];
  assign rs = instr[25:21];
  assign rt = instr[20:16];

  // Other names for the same wires on the sheet: _31_26[5:0] = instr[31:26]; _5_0[5:0] = instr[5:0];
  //   _10_6[4:0] = instr[10:6]; _15_11[4:0] = instr[15:11]; _20_16[4:0] = instr[20:16]; _25_21[4:0] = instr[25:21]
endmodule

module test (
  output [31:0] Instr,
  output [31:0] PC,
  output RegWrite,
  output [4:0] RegAddr,
  output [31:0] RegData,
  output halt,
  output MemWrite,
  output [31:0] MemAddr,
  output [31:0] MemData
);

  wire clock_1_out, comparator_1_gt;
  wire [15:0] counter_1_q;

  Clock clock_1 (.out(clock_1_out));
  Counter #(.width(16), .max('hffff), .ongoal("stay")) counter_1 (
    .Q(counter_1_q), .carry(halt), .clk(clock_1_out));  // open: load, D, count, clr
  Comparator #(.width(16), .mode("unsigned")) comparator_1 (
    .a({16{1'b0}}), .b(counter_1_q), .gt(comparator_1_gt));  // open: eq, lt
  main main (
    .reset(comparator_1_gt), .Instr(Instr), .PC(PC), .RegWrite(RegWrite), .RegAddr(RegAddr),
    .RegData(RegData), .MemWrite(MemWrite), .MemAddr(MemAddr), .MemData(MemData));
endmodule
