// Logisim project testbench.circ as structural Verilog: 1 circuit, main circuit testbenchA
module testbenchA (
  output [31:0] Instr,
  output [31:0] PC,
  output RegWrite,
  output [4:0] RegAddr,
  output [31:0] RegData,
  output halt,
  output MemWrite,
  output [31:0] MemAddr,
  output [31:0] MemData
);

  wire clock_1_out, comparator_1_gt;
  wire [12:0] counter_1_q;

  Clock clock_1 (.out(clock_1_out));
  Counter #(.width(13), .max('h1fff), .ongoal("stay")) counter_1 (
    .Q(counter_1_q), .carry(halt), .clk(clock_1_out));  // open: load, D, count, clr
  Comparator #(.width(13), .mode("unsigned")) comparator_1 (
    .a({13{1'b0}}), .b(counter_1_q), .gt(comparator_1_gt));  // open: eq, lt
  // cpuA_main main: pin names not known; wires that end beside it: comparator_1_gt, Instr, PC, RegWrite, RegAddr, RegData, MemWrite, MemAddr, MemData
endmodule
