// Logisim project p3_cpu.circ as structural Verilog: 10 circuits, main circuit main
module main (
  input  reset,
  output [31:0] Instr,
  output [31:0] PC,
  output RegWriteOut,
  output [4:0] RegAddr,
  output [31:0] RegData,
  output MemWrite,
  output [31:0] MemAddr,
  output [31:0] MemData
);

  wire ALUSrc, and_1_out, and_2_out, Branch, \byte , clk_out, ExtOp, half, isSigned, Jump, JumpReturn, Link,
       MemRead, MemToReg, \new , RegDst, RegWrite, ZeroSign;
  wire [3:0] ALUop;
  wire [4:0] multiplexer_1_out, multiplexer_2_out, rd, rs, rt, s;
  wire [5:0] funct, opCode;
  wire [15:0] immediate;
  wire [25:0] instr_index;
  wire [31:0] dm_1_out, extended, grf_1_rd1, multiplexer_5_out, multiplexer_6_out, nPC;

  Clock clk (.out(clk_out));
  and and_1 (and_1_out, ZeroSign, Branch);
  extend extend_1 (.in(immediate), .op(ExtOp), .out(extended));
  ifu ifu_1 (
    .clk(clk_out), .reset(reset), .doBranch(and_1_out), .offset(immediate), .Jump(Jump),
    .instr_index(instr_index), .PC_from_jr(RegData), .PCsource(JumpReturn), .curPC(PC), .nextPC(nPC),
    .instr(Instr));
  control control_1 (
    .op(opCode), .funct(funct), .RegDst(RegDst), .ALUSrc(ALUSrc), .MemToReg(MemToReg), .RegWrite(RegWrite),
    .MemRead(MemRead), .MemWrite(MemWrite), .Branch(Branch), .ExtOp(ExtOp), .Jump(Jump), .Link(Link),
    .JumpReturn(JumpReturn), .\byte (\byte ), .half_word(half), .load_signed(isSigned), .ALUOp(ALUop),
    .\new (\new ));
  instr_decode instr_decode_1 (
    .instr(Instr), .opCode(opCode), .funct(funct), .immediate(immediate), .instr_index(instr_index), .rs(rs),
    .rt(rt), .rd(rd), .s(s));
  Multiplexer #(.width(5)) multiplexer_1 (.in0(rt), .in1(rd), .out(multiplexer_1_out), .sel(RegDst));  // open: en
  Multiplexer #(.width(5)) multiplexer_2 (
    .in0(multiplexer_1_out), .in1({5{1'b1}}), .out(multiplexer_2_out), .sel(Link));  // open: en
  Multiplexer #(.width(5)) multiplexer_3 (.in0(multiplexer_2_out), .in1(rs), .out(RegAddr), .sel(1'b0));  // open: en
  // Probe on Instr
  // Probe on PC
  or or_1 (RegWriteOut, RegWrite, and_2_out);
  grf grf_1 (
    .A1(rs), .A2(rt), .A3(RegAddr), .WD(RegData), .RD1(grf_1_rd1), .RD2(MemData), .clk(clk_out),
    .reset(reset), .WE(RegWriteOut));
  Multiplexer #(.width(32)) multiplexer_4 (
    .in0(multiplexer_6_out), .in1(dm_1_out), .out(RegData), .sel(MemToReg));  // open: en
  // Probe on nPC
  and and_2 (and_2_out, \new , 1'b0);
  Multiplexer #(.width(32)) multiplexer_5 (
    .in0(MemData), .in1(extended), .out(multiplexer_5_out), .sel(ALUSrc));  // open: en
  Multiplexer #(.width(32)) multiplexer_6 (.in0(MemAddr), .in1(nPC), .out(multiplexer_6_out), .sel(Link));  // open: en
  alu alu_1 (.A(grf_1_rd1), .B(multiplexer_5_out), .S(s), .op(ALUop), .zero(ZeroSign), .out(MemAddr));
  dm dm_1 (
    .clk(clk_out), .reset(reset), .write_enable(MemWrite), .read_enable(MemRead), .\byte (\byte ),
    .half_word(half), .extOp(isSigned), .read_address(MemAddr), .write_data(MemData), .out(dm_1_out));
endmodule

module grf (
  input  clk,
  input  reset,
  input  WE,
  input  [4:0] A1,
  input  [4:0] A2,
  input  [4:0] A3,
  input  [31:0] WD,
  output [31:0] RD1,
  output [31:0] RD2
);

  wire [31:0] in0, in1, in2, in3, in4, in5, in6, in7, in8, in9, in10, in11, in12, in13, in14, in15, in16,
       in17, in18, in19, in20, in21, in22, in23, in24, in25, in26, in27, in28, in29, in30, in31, val0, val1,
       val2, val3, val4, val5, val6, val7, val8, val9, val10, val11, val12, val13, val14, val15, val16,
       val17, val18, val19, val20, val21, val22, val23, val24, val25, val26, val27, val28, val29, val30,
       val31;

  Demultiplexer #(.select(5), .width(32), .tristate("true")) demultiplexer_1 (
    .out0(in0), .out1(in1), .out2(in2), .out3(in3), .out4(in4), .out5(in5), .out6(in6), .out7(in7),
    .out8(in8), .out9(in9), .out10(in10), .out11(in11), .out12(in12), .out13(in13), .out14(in14),
    .out15(in15), .out16(in16), .out17(in17), .out18(in18), .out19(in19), .out20(in20), .out21(in21),
    .out22(in22), .out23(in23), .out24(in24), .out25(in25), .out26(in26), .out27(in27), .out28(in28),
    .out29(in29), .out30(in30), .out31(in31), .in(WD), .sel(A3));  // open: en
  Register #(.width(32)) register_1 (.D({32{1'b0}}), .en(WE), .Q(val0), .clk(clk), .clr(reset));
  Register #(.width(32)) register_2 (.D(in1), .en(WE), .Q(val1), .clk(clk), .clr(reset));
  Register #(.width(32)) register_3 (.D(in2), .en(WE), .Q(val2), .clk(clk), .clr(reset));
  Register #(.width(32)) register_4 (.D(in3), .en(WE), .Q(val3), .clk(clk), .clr(reset));
  Register #(.width(32)) register_5 (.D(in4), .en(WE), .Q(val4), .clk(clk), .clr(reset));
  Register #(.width(32)) register_6 (.D(in20), .en(WE), .Q(val20), .clk(clk), .clr(reset));
  Register #(.width(32)) register_7 (.D(in21), .en(WE), .Q(val21), .clk(clk), .clr(reset));
  Register #(.width(32)) register_8 (.D(in22), .en(WE), .Q(val22), .clk(clk), .clr(reset));
  Register #(.width(32)) register_9 (.D(in5), .en(WE), .Q(val5), .clk(clk), .clr(reset));
  Register #(.width(32)) register_10 (.D(in6), .en(WE), .Q(val6), .clk(clk), .clr(reset));
  Register #(.width(32)) register_11 (.D(in7), .en(WE), .Q(val7), .clk(clk), .clr(reset));
  Register #(.width(32)) register_12 (.D(in8), .en(WE), .Q(val8), .clk(clk), .clr(reset));
  Register #(.width(32)) register_13 (.D(in9), .en(WE), .Q(val9), .clk(clk), .clr(reset));
  Register #(.width(32)) register_14 (.D(in23), .en(WE), .Q(val23), .clk(clk), .clr(reset));
  Register #(.width(32)) register_15 (.D(in24), .en(WE), .Q(val24), .clk(clk), .clr(reset));
  Register #(.width(32)) register_16 (.D(in25), .en(WE), .Q(val25), .clk(clk), .clr(reset));
  Register #(.width(32)) register_17 (.D(in10), .en(WE), .Q(val10), .clk(clk), .clr(reset));
  Register #(.width(32)) register_18 (.D(in11), .en(WE), .Q(val11), .clk(clk), .clr(reset));
  Register #(.width(32)) register_19 (.D(in12), .en(WE), .Q(val12), .clk(clk), .clr(reset));
  Register #(.width(32)) register_20 (.D(in13), .en(WE), .Q(val13), .clk(clk), .clr(reset));
  Register #(.width(32)) register_21 (.D(in14), .en(WE), .Q(val14), .clk(clk), .clr(reset));
  Register #(.width(32)) register_22 (.D(in26), .en(WE), .Q(val26), .clk(clk), .clr(reset));
  Register #(.width(32)) register_23 (.D(in27), .en(WE), .Q(val27), .clk(clk), .clr(reset));
  Register #(.width(32)) register_24 (.D(in28), .en(WE), .Q(val28), .clk(clk), .clr(reset));
  Register #(.width(32)) register_25 (.D(in15), .en(WE), .Q(val15), .clk(clk), .clr(reset));
  Register #(.width(32)) register_26 (.D(in16), .en(WE), .Q(val16), .clk(clk), .clr(reset));
  Register #(.width(32)) register_27 (.D(in17), .en(WE), .Q(val17), .clk(clk), .clr(reset));
  Register #(.width(32)) register_28 (.D(in18), .en(WE), .Q(val18), .clk(clk), .clr(reset));
  Register #(.width(32)) register_29 (.D(in19), .en(WE), .Q(val19), .clk(clk), .clr(reset));
  Register #(.width(32)) register_30 (.D(in29), .en(WE), .Q(val29), .clk(clk), .clr(reset));
  Register #(.width(32)) register_31 (.D(in30), .en(WE), .Q(val30), .clk(clk), .clr(reset));
  Register #(.width(32)) register_32 (.D(in31), .en(WE), .Q(val31), .clk(clk), .clr(reset));
  Multiplexer #(.select(5), .width(32)) multiplexer_1 (
    .in0(val0), .in1(val1), .in2(val2), .in3(val3), .in4(val4), .in5(val5), .in6(val6), .in7(val7),
    .in8(val8), .in9(val9), .in10(val10), .in11(val11), .in12(val12), .in13(val13), .in14(val14),
    .in15(val15), .in16(val16), .in17(val17), .in18(val18), .in19(val19), .in20(val20), .in21(val21),
    .in22(val22), .in23(val23), .in24(val24), .in25(val25), .in26(val26), .in27(val27), .in28(val28),
    .in29(val29), .in30(val30), .in31(val31), .out(RD1), .sel(A1));  // open: en
  Multiplexer #(.select(5), .width(32)) multiplexer_2 (
    .in0(val0), .in1(val1), .in2(val2), .in3(val3), .in4(val4), .in5(val5), .in6(val6), .in7(val7),
    .in8(val8), .in9(val9), .in10(val10), .in11(val11), .in12(val12), .in13(val13), .in14(val14),
    .in15(val15), .in16(val16), .in17(val17), .in18(val18), .in19(val19), .in20(val20), .in21(val21),
    .in22(val22), .in23(val23), .in24(val24), .in25(val25), .in26(val26), .in27(val27), .in28(val28),
    .in29(val29), .in30(val30), .in31(val31), .out(RD2), .sel(A2));  // open: en
endmodule

module extend (
  input  [15:0] in,
  input  op,
  output [31:0] out
);

  wire [31:0] bit_extender_1_out, bit_extender_2_out;

  assign bit_extender_1_out = {{16{1'b0}}, in};  // Bit_Extender bit_extender_1
  assign bit_extender_2_out = {{16{in[15]}}, in};  // Bit_Extender bit_extender_2
  Multiplexer #(.width(32)) multiplexer_1 (
    .in0(bit_extender_1_out), .in1(bit_extender_2_out), .out(out), .sel(op));  // open: en
endmodule

module dm (
  input  clk,
  input  reset,
  input  write_enable,
  input  read_enable,
  input  \byte ,
  input  half_word,
  input  extOp,
  input  [31:0] read_address,
  input  [31:0] write_data,
  output [31:0] out
);

  wire [7:0] multiplexer_1_out;
  wire [15:0] multiplexer_2_out;
  wire [31:0] _32_out, bit_extender_1_out, bit_extender_2_out, bit_extender_3_out, bit_extender_4_out,
       byte_out, half_out, multiplexer_5_out;

  Multiplexer #(.select(2), .width(8)) multiplexer_1 (
    .in0(_32_out[7:0]), .in1(_32_out[15:8]), .in2(_32_out[23:16]), .in3(_32_out[31:24]),
    .out(multiplexer_1_out), .sel(read_address[1:0]));  // open: en
  Multiplexer #(.width(16)) multiplexer_2 (
    .in0(_32_out[15:0]), .in1(_32_out[31:16]), .out(multiplexer_2_out), .sel(read_address[1]));  // open: en
  assign bit_extender_1_out = {{24{1'b0}}, multiplexer_1_out};  // Bit_Extender bit_extender_1
  assign bit_extender_2_out = {{24{multiplexer_1_out[7]}}, multiplexer_1_out};  // Bit_Extender bit_extender_2
  assign bit_extender_3_out = {{16{1'b0}}, multiplexer_2_out};  // Bit_Extender bit_extender_3
  assign bit_extender_4_out = {{16{multiplexer_2_out[15]}}, multiplexer_2_out};  // Bit_Extender bit_extender_4
  Multiplexer #(.width(32)) multiplexer_3 (
    .in0(bit_extender_1_out), .in1(bit_extender_2_out), .out(byte_out), .sel(extOp));  // open: en
  Multiplexer #(.width(32)) multiplexer_4 (
    .in0(bit_extender_3_out), .in1(bit_extender_4_out), .out(half_out), .sel(extOp));  // open: en
  RAM #(.addrWidth(16), .dataWidth(32), .bus("separate")) ram_1 (
    .addr(read_address[17:2]), .din(write_data), .data(_32_out), .str(write_enable), .sel(1'b1), .clk(clk),
    .ld(read_enable), .clr(reset));
  Multiplexer #(.width(32)) multiplexer_5 (
    .in0(_32_out), .in1(byte_out), .out(multiplexer_5_out), .sel(\byte ));  // open: en
  Multiplexer #(.width(32)) multiplexer_6 (
    .in0(multiplexer_5_out), .in1(half_out), .out(out), .sel(half_word));  // open: en

  // Other names for the same wires on the sheet: which_byte[1:0] = read_address[1:0]; which_half = read_address[1]
endmodule

module alu (
  input  [31:0] A,
  input  [31:0] B,
  input  [4:0] S,
  input  [3:0] op,
  output zero,
  output [31:0] out
);

  wire [31:0] adder_1_out, adder_2_out, or_1_out, shifter_1_out, shifter_2_out, subtractor_1_out;

  Adder #(.width(32)) adder_1 (.a(A), .b(B), .out(adder_1_out));  // open: cin, cout
  Subtractor #(.width(32)) subtractor_1 (.a(A), .b(B), .out(subtractor_1_out));  // open: bin, bout
  assign or_1_out = A | B;  // OR_Gate or_1, 32 bits wide
  Shifter #(.width(32)) shifter_1 (.in(B), .\dist (S), .out(shifter_1_out));
  Shifter #(.width(32)) shifter_2 (.in(B), .\dist (5'b10000), .out(shifter_2_out));
  Adder #(.width(32)) adder_2 (.a(B), .b(32'h4), .out(adder_2_out));  // open: cin, cout
  Multiplexer #(.select(4), .width(32)) multiplexer_1 (
    .in0(adder_1_out), .in1(subtractor_1_out), .in2(or_1_out), .in3(shifter_1_out), .in4(shifter_2_out),
    .in5(adder_2_out), .in6(A), .out(out), .sel(op));  // open: in7, in8, in9, in10, in11, in12, in13, in14, in15, en
  Comparator #(.width(32)) comparator_1 (.a({32{1'b0}}), .b(out), .eq(zero));  // open: gt, lt
endmodule

module ifu (
  input  clk,
  input  reset,
  input  doBranch,
  input  [15:0] offset,
  input  Jump,
  input  [25:0] instr_index,
  input  [31:0] PC_from_jr,
  input  PCsource,
  output [31:0] curPC,
  output [31:0] nextPC,
  output [31:0] instr
);

  wire [11:0] bitselector_1_out;
  wire [31:0] offset_t, register_1_q, shifter_1_out, subtractor_1_out;

  Subtractor #(.width(32)) subtractor_1 (.a(nextPC), .b(32'h3000), .out(subtractor_1_out));  // open: bin, bout
  assign offset_t = {{14{offset[15]}}, {offset, 2'b00}};  // Bit_Extender bit_extender_1
  Register #(.width(32)) register_1 (.D(subtractor_1_out), .Q(register_1_q), .clk(clk), .clr(reset));  // open: en
  Adder #(.width(32)) adder_1 (.a(register_1_q), .b(32'h3000), .out(curPC));  // open: cin, cout
  Shifter #(.width(32), .shift("lr")) shifter_1 (.in(register_1_q), .\dist (5'b00010), .out(shifter_1_out));
  nextPC nextpc_1 (
    .curPC(register_1_q), .offset(offset_t), .doBranch(doBranch), .Jump(Jump), .PCsource(PCsource),
    .nextPC(nextPC), .instr_index({curPC[31:28], instr_index, 2'b00}), .PC_from_jr(PC_from_jr));
  BitSelector #(.width(32), .group(12)) bitselector_1 (.in(shifter_1_out), .out(bitselector_1_out), .sel(2'b00));
  ROM #(.addrWidth(12), .dataWidth(32)) rom_1 (.addr(bitselector_1_out), .data(instr), .sel(1'b1));

  // Other names for the same wires on the sheet: instr_index_t[31:2] = {curPC[31:28], instr_index}

  // Notes on the sheet:
  //   contents of rom_1 (hex, n*v repeats v):
  //   34020000 34091000 34032000 34071090 3404ffff 3405ffff 3406aaaa 34085678 340aaaaa 340b1234 340c0001
  //   340d0001 340e1234 340fffff 3410ffff 3411ffff 34125678 34135678 3414aaaa 3415aaaa 34160001 34171234
  //   3418ffff 34191234 341aaaaa 341baaaa 341cffff 341dffff 341eaaaa 341f1234 ac7c0000 3c19aa6d ad39009c
  //   acf00034 8c400000 8d3cff00 ad2f0000 acfd0000 ac6efe70 3678c9c4 ac5f0000 ac7dff10 8cf4ff64 ac58fffc
  //   8c700000 8c72ffe8 acf00064 3c0d2176 3c150000 ac5c007c 36a4ca31 ac44fffc 8c450000 ad30fe64 ac5d007c
  //   8d2aff38 ad2e01cc ace3ff6c 8d2bff60 350ab293 ac570000 37385cf4 8c760030 ac47014c 8d310000 12700147
  //   8c5f0174 8c7dff9c 36fa72c7 345d6e18 ad260000 8c680174 8d3e0000 0 3710054e 374e570b 11fd00a8 ac570000
  //   8c640000 acec01c8 ad3a0000 8d3ffe60 ac4d0000 3525f81d 8c6b0068 8cec00c4 3c105109 ac7d0130 8ced0000
  //   3715ac06 34e56c24 3c1a0000 ad23ffb4 8d20fee4 ac68ff34 130c0133 8ceafef4 ad33fec8 ac59fffc 0 8c6f0014
  //   37957ebd 8d3f00b0 8d3bff3c 8d3c0000 ad3efef4 3c18b2fc 8d2dfe64 8cfd0094 ace3017c 8d3d0000 ad35fe60
  //   37eb6d03 8d20ffbc ace901c4 ac5cfffc ad26fe9c ac4f0000 ac530000 ac580160 8d2a0074 ace601d8 ad2d0090
  //   8d34feb8 8d38fe70 ac750180 acf4ff44 ac4cfffc 8c64ff78 ad3fffe8 8d3c01ec 8d24fff0 345a93ea 34576f6d
  //   8cfe0000 3511ffff 8c40fffc 8c6500bc aced01a8 8c5e002c 8ce5ffac ac520000 0 8c600000 ac720000 8c4afffc
  //   8c40fffc 8c5c010c 8c500000 ac5afffc 3c06ea06 3664c4cf 8d2dfe50 3651d28e 3c0b0000 3c167243 8c5c01e0
  //   8d390000 36b7de7e ac53fffc 357f6f1e ac46fffc 8d2d0000 ad25ff04 3472fffd acff0000 8c78fe28 8c750000
  //   37aa1c03 ac5b009c ad23fef4 8c4b010c 10c8002e ac7e00ac ac7a0108 8c550000 8c4e0134 8c680148 8cf5007c
  //   8cf7ffcc ace90000 ac45fffc acef0000 8ce8feec 361fdca4 ac73ff2c acf4019c acf80000 8d2cfe94 8cfb0000
  //   8c4dfffc 3715663e ace60068 3c08bffc ac530000 8d390194 ac42fffc 34e8bdd7 ac6bfe0c ace60188 ac720000
  //   347b5c16 ad220000 ac69fe30 ac650000 8c5cfffc ac660000 8c56fffc 8c760090 109effc1 3734ffff ad2f016c
  //   365796ad 352bdb87 36301dc2 ac78ffb8 349c0002 3457f528 8c46fffc 0 3c144f87 10ce0097 354dffff 352cfffe
  //   ad2d01b0 ace3013c 8d3efe58 ac4efffc ac52fffc ac75fe5c 371ea730 8cff0000 8c730000 3c1462a4 35b20000
  //   ad3f00f4 8c5bfffc 350fbfb8 ad3701c4 acf6ff50 8d3b00ac 8d2afef4 8d2ffef0 36b40002 ac7ffec0 10960176
  //   8c400000 8c7b0000 37d2d248 3c1f3968 ad3f0120 8c5efffc 8cf1fed4 349d5253 8c5701a8 ac4d00b0 350ff39f
  //   356a7fd7 8c4afffc 8c70ffd8 3699fffe 8c79ff60 8ce60000 36bf46d4 3c0ea65d 8c59fffc ad3b00d8 ac5e00b4
  //   3c11fffd 8c730000 8c52fffc 8c590000 8ce80194 363065db 8cf100bc 8d3b007c 8d200118 ac780000 ac560000
  //   acec0104 ad3b0000 1210ff73 8d250000 ac5efffc 8d3f0000 3c14571d 8cea0000 8c4efffc 351fde44 12940052
  //   ac4cfffc 8c5f0160 11160168 35e40001 8c7cffe8 8cf1ff7c ac720118 acf40000 36fbf5f9 8c6b0000 3697fffe
  //   8c6fff44 8c5a00a4 acf30000 8c6a00e8 3c11b93b 8d3b0004 8c540000 111fff9b 8d3ffeec 8ceefef4 8c590000
  //   8d30fe98 ad32012c 3c0ed56e 3c17c966 ad3900e0 ac5d014c ad30ff18 3c0a4e76 8d2f0100 ad380000 355e7368
  //   ac69feb0 36561c72 3792e35b 8c770000 ad220114 3c0b0f4d 8c6b0000 8c740000 acf0fed8 ad220000 35db0a47
  //   acff0000 ac4d0068 36ec0514 ac5b0140 acef0000 12f2014e acf4ff1c 8cf00000 ad240034 ac460084 ad280000
  //   ac5a0000 0 3c050001 8c70fef4 34af1898 111f009a 8c6001c8 8c4f00e0 12cb00f4 361ebe35 369f5d61 ad260000
  //   3c060e63 0 ac78019c 0 8c5e0000 8c4c0008 8c5bfffc 10f40041 371e3f57 8c4e0154 36dfddf5 3488ffff
  //   acedfe38 8c770000 ac77fef0 36ca4050 8d250000 8c740138 8d24fedc ac470000 ac71febc 8d2f0000 8c4bfffc
  //   acf6ffac acfb0000 36450001 ac430000 ac450108 8d36018c ac7d0000 12e4ffaf 8ced01ac ac790000 8c56fffc
  //   8c710000 8c5000ac 3c058cc1 ac6f00c8 375ea411 8d2b0124 ace40000 8c520128 ac4ffffc 8d390080 8c680000
  //   34d92f33 367f6c76 ac510000 3c110000 acfd0000 8d2000c8 353f126b ace700f0 36387a65 ac6e0000 8c48fffc
  //   8cfdfef8 ac480000 8d330000 36cab6e3 0 3c1ca246 8c5900a4 8c65ff28 ac520104 ace40134 8d260184 34ff860e
  //   8c5cfffc 8c6f0088 8c7b0000 112bffaa 8d350190 acf300f0 34799e27 0 ac580038 ad26feb0 ac7d0000 ad2e0000
  //   35cbc846 acf40000 ac4bfffc ad23fe90 acf60000 3c1d9a52 8c7e0070 8c4b0000 0 ac780000 ac6301b4 ace4feb0
  //   3c0da542 8c52fffc ac43fffc ad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
endmodule

module control (
  input  [5:0] op,
  input  [5:0] funct,
  output RegDst,
  output ALUSrc,
  output MemToReg,
  output RegWrite,
  output MemRead,
  output MemWrite,
  output Branch,
  output ExtOp,
  output Jump,
  output Link,
  output JumpReturn,
  output \byte ,
  output half_word,
  output load_signed,
  output \new ,
  output [3:0] ALUOp
);

  wire add, beq, j, jal, jr, lb, lh, lui, lw, nop, not_1_out, not_2_out, not_3_out, not_4_out, not_5_out,
       not_6_out, not_7_out, not_8_out, not_9_out, not_10_out, not_11_out, not_12_out, not_13_out,
       not_14_out, not_15_out, not_16_out, not_17_out, not_18_out, not_19_out, not_20_out, not_21_out,
       not_22_out, not_23_out, not_24_out, not_25_out, not_26_out, not_27_out, not_28_out, not_29_out,
       not_30_out, not_31_out, not_32_out, not_33_out, not_34_out, not_35_out, not_36_out, not_37_out,
       not_38_out, not_39_out, not_40_out, not_41_out, not_42_out, not_43_out, not_44_out, not_45_out,
       not_46_out, not_47_out, not_48_out, not_49_out, not_50_out, not_51_out, not_52_out, not_53_out,
       not_54_out, not_55_out, not_56_out, not_57_out, not_58_out, not_59_out, not_60_out, not_61_out,
       not_62_out, not_63_out, not_64_out, not_65_out, ori, sll, special, sub, sw;
  wire [15:0] or_1_out;

  or or_1 (or_1_out[0], add, lw, sw);
  or or_2 (or_1_out[1], sub, beq);
  buf or_3 (or_1_out[2], ori);  // OR_Gate
  or or_4 (or_1_out[3], nop, sll);
  buf or_5 (or_1_out[4], lui);  // OR_Gate
  buf or_6 (or_1_out[5], jal);  // OR_Gate
  buf or_7 (or_1_out[6], jr);  // OR_Gate
  not not_1 (not_1_out, op[5]);
  not not_2 (not_2_out, op[4]);
  not not_3 (not_3_out, op[3]);
  and u_special (special, not_1_out, not_2_out, not_3_out, not_4_out, not_5_out, not_6_out);
  not not_4 (not_4_out, op[2]);
  not not_5 (not_5_out, op[1]);
  not not_6 (not_6_out, op[0]);
  not not_7 (not_7_out, op[5]);
  not not_8 (not_8_out, op[4]);
  and u_ori (ori, not_7_out, not_8_out, op[3], op[2], not_9_out, op[0]);
  not not_9 (not_9_out, op[1]);
  not not_10 (not_10_out, op[4]);
  not not_11 (not_11_out, op[3]);
  and u_lw (lw, op[5], not_10_out, not_11_out, not_12_out, op[1], op[0]);
  not not_12 (not_12_out, op[2]);
  not not_13 (not_13_out, op[4]);
  and u_sw (sw, op[5], not_13_out, op[3], not_14_out, op[1], op[0]);
  not not_14 (not_14_out, op[2]);
  not not_15 (not_15_out, op[5]);
  not not_16 (not_16_out, op[4]);
  not not_17 (not_17_out, op[3]);
  and u_beq (beq, not_15_out, not_16_out, not_17_out, op[2], not_18_out, not_19_out);
  not not_18 (not_18_out, op[1]);
  not not_19 (not_19_out, op[0]);
  not not_20 (not_20_out, op[5]);
  not not_21 (not_21_out, op[4]);
  and u_lui (lui, not_20_out, not_21_out, op[3], op[2], op[1], op[0]);
  not not_22 (not_22_out, op[5]);
  not not_23 (not_23_out, op[4]);
  not not_24 (not_24_out, op[3]);
  and u_j (j, not_22_out, not_23_out, not_24_out, not_25_out, op[1], not_26_out);
  not not_25 (not_25_out, op[2]);
  not not_26 (not_26_out, op[0]);
  not not_27 (not_27_out, op[5]);
  not not_28 (not_28_out, op[4]);
  not not_29 (not_29_out, op[3]);
  and u_jal (jal, not_27_out, not_28_out, not_29_out, not_30_out, op[1], op[0]);
  not not_30 (not_30_out, op[2]);
  not not_31 (not_31_out, op[4]);
  not not_32 (not_32_out, op[3]);
  and u_lb (lb, op[5], not_31_out, not_32_out, not_33_out, not_34_out, not_35_out);
  not not_33 (not_33_out, op[2]);
  not not_34 (not_34_out, op[1]);
  not not_35 (not_35_out, op[0]);
  not not_36 (not_36_out, op[4]);
  not not_37 (not_37_out, op[3]);
  and u_lh (lh, op[5], not_36_out, not_37_out, not_38_out, not_39_out, op[0]);
  not not_38 (not_38_out, op[2]);
  not not_39 (not_39_out, op[1]);
  BitFinder #(.width(16)) bitfinder_1 (.in(or_1_out), .index(ALUOp));  // open: found
  or or_8 (RegDst, add, sub, nop, sll);
  or or_9 (MemToReg, lw, lb, lh);
  or or_10 (RegWrite, add, sub, ori, lw, lui, nop, sll, lb, lh);
  or or_11 (MemRead, lw, lb);
  buf or_12 (MemWrite, sw);  // OR_Gate
  buf or_13 (Branch, beq);  // OR_Gate
  or or_14 (ExtOp, lw, sw);
  buf or_15 (Jump, j);  // OR_Gate
  buf or_16 (Link, jal);  // OR_Gate
  buf or_17 (JumpReturn, jr);  // OR_Gate
  buf or_18 (\byte , lb);  // OR_Gate
  buf or_19 (half_word, lh);  // OR_Gate
  or or_20 (load_signed, lb, lh);
  not not_40 (not_40_out, funct[4]);
  not not_41 (not_41_out, funct[3]);
  and u_add (add, funct[5], not_40_out, not_41_out, special, not_42_out, not_43_out, not_44_out);
  not not_42 (not_42_out, funct[2]);
  not not_43 (not_43_out, funct[1]);
  not not_44 (not_44_out, funct[0]);
  not not_45 (not_45_out, funct[4]);
  not not_46 (not_46_out, funct[3]);
  and u_sub (sub, funct[5], not_45_out, not_46_out, special, not_47_out, funct[1], not_48_out);
  not not_47 (not_47_out, funct[2]);
  not not_48 (not_48_out, funct[0]);
  not not_49 (not_49_out, funct[5]);
  not not_50 (not_50_out, funct[4]);
  not not_51 (not_51_out, funct[3]);
  and u_nop (nop, not_49_out, not_50_out, not_51_out, special, not_52_out, not_53_out, not_54_out);
  not not_52 (not_52_out, funct[2]);
  not not_53 (not_53_out, funct[1]);
  not not_54 (not_54_out, funct[0]);
  not not_55 (not_55_out, funct[5]);
  not not_56 (not_56_out, funct[4]);
  not not_57 (not_57_out, funct[3]);
  and u_sll (sll, not_55_out, not_56_out, not_57_out, special, not_58_out, not_59_out, not_60_out);
  not not_58 (not_58_out, funct[2]);
  not not_59 (not_59_out, funct[1]);
  not not_60 (not_60_out, funct[0]);
  not not_61 (not_61_out, funct[5]);
  not not_62 (not_62_out, funct[4]);
  and u_jr (jr, not_61_out, not_62_out, funct[3], special, not_63_out, not_64_out, not_65_out);
  not not_63 (not_63_out, funct[2]);
  not not_64 (not_64_out, funct[1]);
  not not_65 (not_65_out, funct[0]);
  or or_21 (ALUSrc, ori, lw, sw, lui, jr, lb);

  assign \new  = 1'b0;
endmodule

module instr_decode (
  input  [31:0] instr,
  output [5:0] opCode,
  output [5:0] funct,
  output [15:0] immediate,
  output [25:0] instr_index,
  output [4:0] rs,
  output [4:0] rt,
  output [4:0] rd,
  output [4:0] s
);


  assign funct = instr[5:0];
  assign immediate = instr[15:0];
  assign instr_index = instr[25:0];
  assign opCode = instr[31:26];
  assign rd = instr[15:11];
  assign rs = instr[25:21];
  assign rt = instr[20:16];
  assign s = instr[10:6];

  // Other names for the same wires on the sheet: _31_26[5:0] = instr[31:26]; _5_0[5:0] = instr[5:0];
  //   _10_6[4:0] = instr[10:6]; _15_11[4:0] = instr[15:11]; _20_16[4:0] = instr[20:16]; _25_21[4:0] = instr[25:21]
endmodule

module test (
  output [31:0] Instr,
  output [31:0] PC,
  output RegWrite,
  output [4:0] RegAddr,
  output [31:0] RegData,
  output halt,
  output MemWrite,
  output [31:0] MemAddr,
  output [31:0] MemData
);

  wire clock_1_out, comparator_1_gt;
  wire [15:0] counter_1_q;

  Clock clock_1 (.out(clock_1_out));
  Counter #(.width(16), .max('hffff), .ongoal("stay")) counter_1 (
    .Q(counter_1_q), .carry(halt), .clk(clock_1_out));  // open: load, D, count, clr
  Comparator #(.width(16), .mode("unsigned")) comparator_1 (
    .a({16{1'b0}}), .b(counter_1_q), .gt(comparator_1_gt));  // open: eq, lt
  main main (
    .reset(comparator_1_gt), .Instr(Instr), .PC(PC), .RegWriteOut(RegWrite), .RegAddr(RegAddr),
    .RegData(RegData), .MemWrite(MemWrite), .MemAddr(MemAddr), .MemData(MemData));
endmodule

module nextPC (
  input  [31:0] curPC,
  input  [31:0] instr_index,
  input  [31:0] PC_from_jr,
  input  [31:0] offset,
  input  doBranch,
  input  Jump,
  input  PCsource,
  output [31:0] nextPC
);

  wire [31:0] adder_1_out, adder_2_out, multiplexer_1_out, multiplexer_2_out;

  Adder #(.width(32)) adder_1 (.a(curPC), .b(32'h3004), .out(adder_1_out));  // open: cin, cout
  Adder #(.width(32)) adder_2 (.a(adder_1_out), .b(offset), .out(adder_2_out));  // open: cin, cout
  Multiplexer #(.width(32)) multiplexer_1 (
    .in0(adder_1_out), .in1(adder_2_out), .out(multiplexer_1_out), .sel(doBranch));  // open: en
  Multiplexer #(.width(32)) multiplexer_2 (
    .in0(multiplexer_1_out), .in1(instr_index), .out(multiplexer_2_out), .sel(Jump));  // open: en
  Multiplexer #(.width(32)) multiplexer_3 (
    .in0(multiplexer_2_out), .in1(PC_from_jr), .out(nextPC), .sel(PCsource));  // open: en
endmodule
